# Fritzing sketch wiring_FBV (saved by Fritzing 0.9.4)
breadboards: 1

parts:
  R2 = Resistor [tolerance=±5% resistance=220 package="0603 [SMD]"]
  R1 = Resistor [tolerance=±5% resistance=1k package="1206 [SMD]"]
  R3 = Resistor [tolerance=±5% resistance=220 package=THT]
  U2 = OPTO_DARL_6N138S [part_number=6N138 package=8-smd]
  Bauteil2 = Arduino Mega 2560 (Rev3)
  U5 = RJ45 Jack [package=rj45-8]

nets:
  N1: R2.Pin_0, U2.A
  N2: R2.Pin_1, U5.6
  VCC: R1.Pin_0, R3.Pin_0, U2.VCC, Bauteil2.5V
  N3: R1.Pin_1, U2.VOUT, Bauteil2.D19/RX1
  N4: R3.Pin_1, U5.8
  GND: U2.C, U2.GND, Bauteil2.GND, U5.1
  N5: Bauteil2.D18/TX1, U5.7
  N6: Bauteil2.VIN, U5.2
